# Fritzing sketch TeensyMIDI (saved by Fritzing 0.9.3b)
breadboards: 1

parts:
  SND21 = Rotary Potentiometer (Small) [maximum_resistance=10kΩ package=THT]
  SND22 = Rotary Potentiometer (Small) [maximum_resistance=10kΩ package=THT]
  SND12 = Rotary Potentiometer (Small) [maximum_resistance=10kΩ package=THT]
  TEENSY = Teensy 2.0
  MUX1 = 74HC4051 [package=so16]
  PAN2 = Rotary Potentiometer (Small) [maximum_resistance=10kΩ package=THT]
  PAN1 = Rotary Potentiometer (Small) [maximum_resistance=10kΩ package=THT]
  SND11 = Rotary Potentiometer (Small) [maximum_resistance=10kΩ package=THT]
  MUX2 = 74HC4051 [package=so16]
  VOL1 = Slide Potentiometer [maximum_resistance=10kΩ]
  VOL2 = Slide Potentiometer [maximum_resistance=10kΩ]
  UP = Pushbutton [package="[THT]"]
  RIGHT = Pushbutton [package="[THT]"]
  LEFT = Pushbutton [package="[THT]"]
  DVCE = Pushbutton [package="[THT]"]
  DOWN = Pushbutton [package="[THT]"]
  R1 = Resistor [tolerance=±5% resistance=10k package=THT]
  R2 = Resistor [tolerance=±5% resistance=10k package=THT]
  R3 = Resistor [tolerance=±5% resistance=10k package=THT]
  R4 = Resistor [tolerance=±5% resistance=10k package=THT]
  R5 = Resistor [tolerance=±5% resistance=10k package=THT]

nets:
  5V: SND21.leg1, SND22.leg1, SND12.leg1, TEENSY.VCC, MUX1.VDD, PAN2.leg1, PAN1.leg1, SND11.leg1, MUX2.VDD, VOL1.leg1, VOL2.leg1, UP.Pin_3, UP.Pin_4, RIGHT.Pin_3, RIGHT.Pin_4, LEFT.Pin_3, LEFT.Pin_4, DVCE.Pin_3, DVCE.Pin_4, DOWN.Pin_3, DOWN.Pin_4
  N1: SND21.wiper, MUX1.IO2
  GND: SND21.leg2, SND22.leg2, SND12.leg2, TEENSY.GND, MUX1.INH, MUX1.VEE, MUX1.VSS, PAN2.leg2, PAN1.leg2, SND11.leg2, MUX2.INH, MUX2.VEE, MUX2.VSS, VOL1.leg2, VOL2.leg2, R1.Pin_0, R2.Pin_0, R3.Pin_0, R4.Pin_0, R5.Pin_0
  N2: SND22.wiper, MUX1.IO1
  N3: SND12.wiper, MUX1.IO6
  N4: TEENSY.B7, MUX1.A, MUX2.A
  N5: TEENSY.C6, MUX1.B, MUX2.B
  N6: TEENSY.C7, MUX1.C, MUX2.C
  N7: TEENSY.F1, MUX2.IO
  N8: TEENSY.F0, MUX1.IO
  N9: MUX1.IO4, SND11.wiper
  N10: MUX1.IO7, PAN1.wiper
  N11: MUX1.IO5, VOL1.wiper
  N12: MUX1.IO3, VOL2.wiper
  N13: MUX1.IO0, PAN2.wiper
  N14: MUX2.IO4, DVCE.Pin_1, DVCE.Pin_2, R1.Pin_1
  N15: MUX2.IO6, LEFT.Pin_1, LEFT.Pin_2, R2.Pin_1
  N16: MUX2.IO7, RIGHT.Pin_1, RIGHT.Pin_2, R3.Pin_1
  N17: MUX2.IO5, UP.Pin_1, UP.Pin_2, R4.Pin_1
  N18: MUX2.IO2, DOWN.Pin_1, DOWN.Pin_2, R5.Pin_1

notes:
  CC32
  CC33
  CC42
  SND12
  CC40
  SND11
  CC36
  PAN1
  CC43
  SND22
  CC41
  SND21
  Not105
  Device
  CC106
  Left
  CC107
  Right
  Track Select/
  Device Select
  Track 1
  Track 2
  CC104
  Up
  CC105
  Down
  Send select
  CC37
  PAN2
